# Fritzing sketch pin_test (saved by Fritzing 1.0.3b)
breadboards: 1

parts:
  Johnny552 = IC, DIP package, 12 pins [chip_label=IC]
  LED1 = smd LED [color="Red (633nm)" package="0805 [SMD]"]
  R1 = Resistor [tolerance=±5% resistance=220 package="0603 [SMD]"]
  R2 = Resistor [tolerance=±5% resistance=220 package="0603 [SMD]"]
  R3 = Resistor [tolerance=±5% resistance=220 package="0603 [SMD]"]
  R4 = Resistor [tolerance=±5% resistance=220 package="0603 [SMD]"]
  R5 = Resistor [tolerance=±5% resistance=220 package="0603 [SMD]"]
  R6 = Resistor [tolerance=±5% resistance=220 package="0603 [SMD]"]
  R7 = Resistor [tolerance=±5% resistance=220 package="0603 [SMD]"]
  R8 = Resistor [tolerance=±5% resistance=220 package="0603 [SMD]"]
  R9 = Resistor [tolerance=±5% resistance=220 package="0603 [SMD]"]
  LED2 = smd LED [color="Red (633nm)" package="0805 [SMD]"]
  LED3 = smd LED [color="Red (633nm)" package="0805 [SMD]"]
  LED4 = smd LED [color="Red (633nm)" package="0805 [SMD]"]
  LED5 = smd LED [color="Green (555nm)" package="0805 [SMD]"]
  LED6 = smd LED [color="Green (555nm)" package="0805 [SMD]"]
  LED7 = smd LED [color="Green (555nm)" package="0805 [SMD]"]
  LED8 = smd LED [color="Green (555nm)" package="0805 [SMD]"]
  LED9 = smd LED [color="Green (555nm)" package="0805 [SMD]"]

nets:
  N1: Johnny552.pin2, R6.Pin_1
  N2: Johnny552.pin3, R7.Pin_1
  N3: Johnny552.pin4, R8.Pin_1
  N4: Johnny552.pin5, R9.Pin_1
  N5: Johnny552.pin7, R4.Pin_0
  N6: Johnny552.pin8, R3.Pin_0
  N7: Johnny552.pin9, R2.Pin_0
  N8: Johnny552.pin10, R1.Pin_0
  N9: Johnny552.pin11, R5.Pin_0
  N10: Johnny552.pin12, LED1.cathode, LED2.cathode, LED3.cathode, LED4.cathode, LED5.cathode, LED6.cathode, LED7.cathode, LED8.cathode, LED9.cathode
  N11: LED1.anode, R9.Pin_0
  N12: R1.Pin_1, LED9.anode
  N13: R2.Pin_1, LED8.anode
  N14: R3.Pin_1, LED7.anode
  N15: R4.Pin_1, LED6.anode
  N16: R5.Pin_1, LED5.anode
  N17: R6.Pin_0, LED2.anode
  N18: R7.Pin_0, LED4.anode
  N19: R8.Pin_0, LED3.anode
