# Fritzing sketch servo_test (saved by Fritzing 1.0.3b)
breadboards: 1

parts:
  Johnny552 = IC, DIP package, 12 pins [chip_label=Johnny552]
  R1 = Resistor [tolerance=±5% resistance=220 package="0603 [SMD]"]
  LED2 = smd LED [color="Green (560nm)" package="0805 [SMD]"]
  J1 = Basic Servo
  J2 = Basic Servo

nets:
  VCC: Johnny552.pin1, J1.vcc, J2.vcc
  N1: Johnny552.pin5, J2.pulse
  N2: Johnny552.pin7, R1.Pin_1
  N3: Johnny552.pin8, J1.pulse
  GND: Johnny552.pin12, LED2.cathode, J1.gnd, J2.gnd
  N4: R1.Pin_0, LED2.anode
